// Logisim project smips.circ as structural Verilog: 4 circuits, main circuit Board
module Board (
);

  wire CLK, HALT, MEM_WE, RESET, TTY_WE;
  wire [3:0] MEM_BE;
  wire [6:0] TTY_DATA;
  wire [31:0] MEM_ADDR, MEM_RDATA, MEM_WDATA;

  Clock Reloj (.out(CLK));
  Button u_Reset (.out(RESET));
  CPU cpu_1 (
    .CLK(CLK), .RESET(RESET), .MEM_RDATA(MEM_RDATA), .MEM_ADDR(MEM_ADDR), .MEM_WDATA(MEM_WDATA),
    .MEM_BE(MEM_BE), .MEM_WE(MEM_WE), .TTY_DATA(TTY_DATA), .TTY_WE(TTY_WE), .HALT(HALT));
  TTY #(.cols(48), .rows(12)) tty_1 (.data(TTY_DATA), .clk(CLK), .we(TTY_WE), .clr(RESET));
  Memory memory_1 (.CLK(CLK), .ADDR(MEM_ADDR), .WDATA(MEM_WDATA), .BE(MEM_BE), .WE(MEM_WE), .RDATA(MEM_RDATA));
  LED u_Halt (.in(HALT));

  // Notes on the sheet:
  //   S-MIPS | Board
  //   No modificar: la CPU se implementa dentro del subcircuito CPU.
endmodule

module CPU (
  input  CLK,
  input  RESET,
  input  [31:0] MEM_RDATA,
  output [31:0] MEM_ADDR,
  output [31:0] MEM_WDATA,
  output [3:0] MEM_BE,
  output MEM_WE,
  output [6:0] TTY_DATA,
  output TTY_WE,
  output HALT
);


  // Notes on the sheet:
  //   CPU S-MIPS: implementar aqui
  //   No cambiar nombres, anchos ni sentido de los pines: la placa depende de ellos.
endmodule

module Memory (
  input  CLK,
  input  [31:0] ADDR,
  input  [31:0] WDATA,
  input  [3:0] BE,
  input  WE,
  output [31:0] RDATA
);

  RAM #(.addrWidth(12), .asyncread("true"), .byteenables("byteEnables"), .dataWidth(32), .\type ("nonvolatile")) Main_Memory (
    .addr(ADDR[13:2]), .we(WE), .oe(1'b1), .clk(CLK), .din(WDATA), .dout(RDATA), .be3(BE[3]), .be2(BE[2]),
    .be1(BE[1]), .be0(BE[0]));

  // Other names for the same wires on the sheet: A[11:0] = ADDR[13:2]

  // Notes on the sheet:
  //   Memoria unificada: 4096 palabras de 32 bits (16 KiB), little-endian
  //   Lectura combinacional; escritura en el flanco de subida de CLK con WE=1, solo en los bytes con BE=1.
  //   Se usan los bits 13..2 de ADDR; los demas se ignoran (el espacio se repite cada 16 KiB).
endmodule

module ALU (
  input  [31:0] A,
  input  [31:0] B,
  input  [2:0] ALU_Op,
  output Zero,
  output [31:0] Result
);

  wire comparator_1_lt;
  wire [31:0] RES_ADD, RES_AND, RES_OR, RES_SLL, RES_SLT, RES_SRL, RES_SUB;

  Adder #(.width(32)) adder_1 (.a(A), .b(B), .out(RES_ADD));  // open: cin, cout
  Subtractor #(.width(32)) subtractor_1 (.a(A), .b(B), .out(RES_SUB));  // open: bin, bout
  assign RES_AND = A & B;  // AND_Gate and_1, 32 bits wide
  assign RES_OR = A | B;  // OR_Gate or_1, 32 bits wide
  Comparator #(.width(32)) comparator_1 (.a(A), .b(B), .lt(comparator_1_lt));  // open: gt, eq
  Shifter #(.width(32)) shifter_1 (.in(A), .\dist (B[4:0]), .out(RES_SLL));
  Shifter #(.shift("lr"), .width(32)) shifter_2 (.in(A), .\dist (B[4:0]), .out(RES_SRL));
  assign RES_SLT = {{31{comparator_1_lt}}, comparator_1_lt};  // Bit_Extender bit_extender_1
  Comparator #(.width(32)) comparator_2 (.a(Result), .b({32{1'b0}}), .eq(Zero));  // open: gt, lt
  Multiplexer #(.select(3), .width(32)) multiplexer_1 (
    .in0(RES_ADD), .in1(RES_SUB), .in2(RES_AND), .in3(RES_OR), .in4(RES_SLT), .in5(RES_SLL), .in6(RES_SRL),
    .out(Result), .sel(ALU_Op));  // open: in7

  // Other names for the same wires on the sheet: SHAMT[4:0] = B[4:0]
endmodule
